// Logisim project dec.circ as structural Verilog: 1 circuit, main circuit main
module main (
  input  [7:0] in_1,
  output [7:0] out_2
);

  Subtractor subtractor_1 (.a(in_1), .b(8'h1), .out(out_2));  // open: bin, bout
endmodule
