// Logisim project inc.circ as structural Verilog: 1 circuit, main circuit inc
module inc (
  input  [7:0] in_1,
  output [7:0] out_2
);

  Adder adder_1 (.a(in_1), .b(8'h1), .out(out_2));  // open: cin, cout
endmodule
