// Logisim project p1-pt1.circ as structural Verilog: 1 circuit, main circuit main
module main (
  input  [15:0] in_1,
  input  [7:0] in_2,
  input  in_3,
  input  in_4,
  input  in_5,
  output [15:0] out_6
);

  wire clock_1_out, not_1_out;

  assign out_6 = in_5 ? in_1 : 16'bz;  // Controlled_Buffer controlled_buffer_1
  RAM #(.dataWidth(16)) ram_1 (.addr(in_2), .data(out_6), .sel(in_3), .clk(clock_1_out), .ld(not_1_out), .clr(in_4));
  not not_1 (not_1_out, in_5);
  Clock clock_1 (.out(clock_1_out));
endmodule
