// Logisim project p1-pt2.circ as structural Verilog: 1 circuit, main circuit main
module main (
  input  in_1,
  input  [7:0] datos,
  input  in_3,
  input  in_4,
  input  [15:0] direcciones,
  output [7:0] salida
);

  wire clock_1_out, nand_1_out, not_1_out, not_2_out, not_3_out;
  wire [7:0] controlled_buffer_1_out, controlled_buffer_2_out, controlled_buffer_4_out, ram_1_data;

  assign controlled_buffer_1_out = not_1_out ? datos : 8'bz;  // Controlled_Buffer controlled_buffer_1
  not not_1 (not_1_out, in_1);
  not not_2 (not_2_out, in_1);
  nand nand_1 (nand_1_out, ~direcciones[8], ~direcciones[9], ~direcciones[10], ~direcciones[11], ~direcciones[12], ~direcciones[13], ~direcciones[14], ~direcciones[15]);  // NAND_Gate
  assign controlled_buffer_2_out = not_2_out ? direcciones[7:0] : 8'bz;  // Controlled_Buffer controlled_buffer_2
  not not_3 (not_3_out, nand_1_out);
  assign salida = not_3_out ? controlled_buffer_1_out : 8'bz;  // Controlled_Buffer controlled_buffer_3
  ROM rom_1 (.addr(controlled_buffer_2_out), .data(controlled_buffer_1_out), .sel(not_3_out));
  assign controlled_buffer_4_out = not_2_out ? controlled_buffer_1_out : 8'bz;  // Controlled_Buffer controlled_buffer_4
  Clock clock_1 (.out(clock_1_out));
  assign salida = nand_1_out ? ram_1_data : 8'bz;  // Controlled_Buffer controlled_buffer_5
  RAM #(.addrWidth(16), .bus("separate")) ram_1 (
    .addr(direcciones), .din(controlled_buffer_4_out), .data(ram_1_data), .str(nand_1_out), .sel(nand_1_out),
    .clk(clock_1_out), .ld(in_3), .clr(in_4));

  // Notes on the sheet:
  //   contents of rom_1 (hex, n*v repeats v):
  //   12 3 23 44 13 0 0 3 34 32 34 bb 34 34 e 5 e4 0 0 4 23 4 0 23 4 4 5 5 4 3 34 5 6 0 4 0 65 4 41 43 65
  //   66 0 78 0 0 fb 0 e6 31 0 5 75 55 34 0 46 7 4 6 1 5 46 0 0 0 35 45 5 6 65 2 34 0 34 54 0 42 34 5 34
endmodule
