// Logisim project p3-final.circ as structural Verilog: 1 circuit, main circuit main
module main (
  input  [7:0] in_1,
  input  [7:0] in_2,
  input  in_3,
  input  [3:0] in_4,
  output out_5,
  output out_6,
  output out_7
);

  wire [7:0] alu_1_out_5;

  Hex_Digit_Display hex_digit_display_1 (.value(alu_1_out_5[7:4]));  // open: dp
  ALU alu_1 (
    .Input_A(in_1), .Input_B(in_2), .Zero_Flag(out_6), .Carry_Flag(out_5), .OP_CODE(in_4), .Overflow(out_7),
    .Cin(in_3), .out_5(alu_1_out_5));
  Hex_Digit_Display hex_digit_display_2 (.value(alu_1_out_5[3:0]));  // open: dp

  // Notes on the sheet:
  //   0000 NOT
  //   0010 OR
  //   0011 XOR
  //   0100 ADD
  //   0101 SUB
  //   0110 ADC
  //   0111 SBB
  //   1000 INC
  //   1001 DEC
  //   1010 SHL
  //   1011 SHR
  //   1100 ROL
  //   1101 ROR
  //   0001 AND
  //   0
endmodule
