// Logisim project p3.circ as structural Verilog: 1 circuit, main circuit ALU
module ALU (
  input  [7:0] Input_A,
  input  [7:0] Input_B,
  input  [3:0] OP_CODE,
  input  Cin,
  output [7:0] out_5,
  output Zero_Flag,
  output Carry_Flag,
  output Overflow
);

  wire adder_1_cout, adder_2_cout, and_1_out, and_2_out, and_3_out, and_6_out, and_7_out, and_8_out,
       and_9_out, comparator_1_eq, or_1_out, subtractor_1_bout, subtractor_2_bout, xor_1_out;
  wire [7:0] adder_1_out, adder_2_out, and_5_out, inc_1_out_2, main_1_out_2, not_1_out, or_2_out,
       shifter_1_out, shifter_2_out, shifter_3_out, shifter_4_out, subtractor_1_out, subtractor_2_out,
       xor_2_out;

  and and_1 (and_1_out, ~OP_CODE[0], ~OP_CODE[1], OP_CODE[2], ~OP_CODE[3]);  // AND_Gate
  and and_2 (and_2_out, OP_CODE[0], ~OP_CODE[1], OP_CODE[2], ~OP_CODE[3]);  // AND_Gate
  Comparator #(.width(1)) comparator_1 (.a(Input_B[7]), .b(Input_A[7]), .eq(comparator_1_eq));  // open: gt, lt
  and and_3 (and_3_out, comparator_1_eq, or_1_out);
  or or_1 (or_1_out, and_1_out, and_2_out);
  xor xor_1 (xor_1_out, Input_A[7], out_5[7]);
  and and_4 (Overflow, and_3_out, xor_1_out);
  assign not_1_out = ~Input_A;  // NOT_Gate not_1, 8 bits wide
  assign and_5_out = Input_A & Input_B;  // AND_Gate and_5, 8 bits wide
  assign or_2_out = Input_A | Input_B;  // OR_Gate or_2, 8 bits wide
  assign xor_2_out = Input_A ^ Input_B;  // XOR_Gate xor_2, 8 bits wide
  Adder adder_1 (.a(Input_A), .b(Input_B), .out(adder_1_out), .cout(adder_1_cout));  // open: cin
  Subtractor subtractor_1 (.a(Input_A), .b(Input_B), .out(subtractor_1_out), .bout(subtractor_1_bout));  // open: bin
  Adder adder_2 (.a(Input_A), .b(Input_B), .out(adder_2_out), .cin(Cin), .cout(adder_2_cout));
  Subtractor subtractor_2 (.a(Input_A), .b(Input_B), .out(subtractor_2_out), .bin(Cin), .bout(subtractor_2_bout));
  Shifter shifter_1 (.in(Input_A), .\dist (Input_B[2:0]), .out(shifter_1_out));
  Shifter #(.shift("lr")) shifter_2 (.in(Input_A), .\dist (Input_B[2:0]), .out(shifter_2_out));
  Shifter #(.shift("rl")) shifter_3 (.in(Input_A), .\dist (Input_B[2:0]), .out(shifter_3_out));
  Shifter #(.shift("rr")) shifter_4 (.in(Input_A), .\dist (Input_B[2:0]), .out(shifter_4_out));
  inc inc_1 (.out_2(inc_1_out_2), .in_1(Input_A));
  dec_main main_1 (.in_1(Input_A), .out_2(main_1_out_2));
  and and_6 (and_6_out, adder_1_cout, ~OP_CODE[0], ~OP_CODE[1], OP_CODE[2], ~OP_CODE[3]);  // AND_Gate
  and and_7 (and_7_out, subtractor_1_bout, OP_CODE[0], ~OP_CODE[1], OP_CODE[2], ~OP_CODE[3]);  // AND_Gate
  and and_8 (and_8_out, adder_2_cout, ~OP_CODE[0], OP_CODE[1], OP_CODE[2], ~OP_CODE[3]);  // AND_Gate
  and and_9 (and_9_out, subtractor_2_bout, OP_CODE[0], OP_CODE[1], OP_CODE[2], ~OP_CODE[3]);  // AND_Gate
  Multiplexer #(.select(4), .width(8)) multiplexer_1 (
    .in0(not_1_out), .in1(and_5_out), .in2(or_2_out), .in3(xor_2_out), .in4(adder_1_out),
    .in5(subtractor_1_out), .in6(adder_2_out), .in7(subtractor_2_out), .in8(inc_1_out_2), .in9(main_1_out_2),
    .in10(shifter_1_out), .in11(shifter_2_out), .in12(shifter_3_out), .in13(shifter_4_out), .out(out_5),
    .sel(OP_CODE));  // open: in14, in15, en
  Comparator comparator_2 (.a(out_5), .b({8{1'b0}}), .eq(Zero_Flag));  // open: gt, lt
  or or_3 (Carry_Flag, and_6_out, and_7_out, and_8_out, and_9_out);
  Hex_Digit_Display hex_digit_display_1 (.value(out_5[3:0]));  // open: dp
  Hex_Digit_Display hex_digit_display_2 (.value(out_5[7:4]));  // open: dp

  // Notes on the sheet:
  //   NOT
  //   AND
  //   OR
  //   XOR
  //   ADD
  //   ADC
  //   SBB
  //   SHL
  //   SHR
  //   SUB
  //   ROL
  //   ROR
  //   OUTPUT
endmodule
