// Logisim project p2-pt1.circ as structural Verilog: 1 circuit, main circuit main
module main (
  input  [7:0] DATOS,
  input  [15:0] DIRECCIONES
);

  wire and_1_out, and_2_out, and_3_out, and_4_out, and_5_out, and_6_out, and_7_out, and_8_out, clock_1_out,
       not_1_out, not_2_out;
  wire [7:0] register_1_q, register_2_q;

  not not_1 (not_1_out, DIRECCIONES[8]);
  not not_2 (not_2_out, DIRECCIONES[9]);
  and and_1 (and_1_out, DIRECCIONES[0], DIRECCIONES[1], DIRECCIONES[2], ~DIRECCIONES[3], DIRECCIONES[4], ~DIRECCIONES[5], ~DIRECCIONES[6], DIRECCIONES[7]);  // AND_Gate
  and and_2 (and_2_out, ~not_1_out, ~not_2_out);  // AND_Gate
  and and_3 (and_3_out, DIRECCIONES[12], DIRECCIONES[13], ~DIRECCIONES[14], DIRECCIONES[15]);  // AND_Gate
  and and_4 (and_4_out, ~and_2_out, DIRECCIONES[10], ~DIRECCIONES[11]);  // AND_Gate
  and and_5 (and_5_out, and_1_out, and_6_out);
  and and_6 (and_6_out, and_2_out, and_3_out);
  and and_7 (and_7_out, and_1_out, and_8_out);
  and and_8 (and_8_out, and_4_out, and_3_out);
  Register register_1 (.D(DATOS), .en(and_5_out), .Q(register_1_q), .clk(clock_1_out));  // open: clr
  Register register_2 (.D(register_1_q), .en(and_7_out), .Q(register_2_q), .clk(clock_1_out));  // open: clr
  Clock clock_1 (.out(clock_1_out));
  Hex_Digit_Display hex_digit_display_1 (.value(register_2_q[3:0]));  // open: dp
  Hex_Digit_Display hex_digit_display_2 (.value(register_2_q[7:4]));  // open: dp
endmodule
