// Logisim project p2-pt2.circ as structural Verilog: 1 circuit, main circuit main
module main (
  input  [7:0] DATOS,
  input  in_2,
  input  [15:0] in_3,
  output [7:0] out_4
);

  wire and_1_out, clock_1_out, nand_1_out;

  Clock clock_1 (.out(clock_1_out));
  nand nand_1 (nand_1_out, ~in_3[0], ~in_3[1], ~in_3[2], ~in_3[3], ~in_3[4], ~in_3[5], ~in_3[6], ~in_3[7], ~in_3[8], ~in_3[9], ~in_3[10], ~in_3[11], ~in_3[12], ~in_3[13], ~in_3[14], ~in_3[15]);  // NAND_Gate
  and and_1 (and_1_out, nand_1_out, in_2);
  D_Flip_Flop d_ff_1 (.clk(clock_1_out), .D(DATOS[0]), .Q(out_4[0]), .en(and_1_out));  // open: Qn, preset, reset
  D_Flip_Flop d_ff_2 (.clk(clock_1_out), .D(DATOS[1]), .Q(out_4[1]), .en(and_1_out));  // open: Qn, preset, reset
  D_Flip_Flop d_ff_3 (.clk(clock_1_out), .D(DATOS[2]), .Q(out_4[2]), .en(and_1_out));  // open: Qn, preset, reset
  D_Flip_Flop d_ff_4 (.clk(clock_1_out), .D(DATOS[3]), .Q(out_4[3]), .en(and_1_out));  // open: Qn, preset, reset
  D_Flip_Flop d_ff_5 (.clk(clock_1_out), .D(DATOS[4]), .Q(out_4[4]), .en(and_1_out));  // open: Qn, preset, reset
  D_Flip_Flop d_ff_6 (.clk(clock_1_out), .D(DATOS[5]), .Q(out_4[5]), .en(and_1_out));  // open: Qn, preset, reset
  D_Flip_Flop d_ff_7 (.clk(clock_1_out), .D(DATOS[6]), .Q(out_4[6]), .en(and_1_out));  // open: Qn, preset, reset
  D_Flip_Flop d_ff_8 (.clk(clock_1_out), .D(DATOS[7]), .Q(out_4[7]), .en(and_1_out));  // open: Qn, preset, reset
endmodule
